// Logisim project PWM signal in logisim..circ as structural Verilog
module _2_1_MUX (
  input  In_0,
  input  In_1,
  input  Select,
  output Out
);

  wire and_1_out, and_2_out, not_1_out;

  not not_1 (not_1_out, Select);
  and and_1 (and_1_out, In_0, not_1_out);
  and and_2 (and_2_out, In_1, Select);
  or or_1 (Out, and_1_out, and_2_out);
endmodule

module _4_1_MUX (
  input  In_00,
  input  In_01,
  input  In_10,
  input  In_11,
  input  Select_1,
  input  Select_0,
  output Out
);

  wire n2_1_mux_1_out, n2_1_mux_2_out;

  _2_1_MUX u_2_1_mux_1 (.In_0(In_01), .In_1(In_00), .Out(n2_1_mux_1_out), .Select(Select_1));
  _2_1_MUX u_2_1_mux_2 (.In_0(In_11), .In_1(In_10), .Out(n2_1_mux_2_out), .Select(Select_1));
  _2_1_MUX u_2_1_mux_3 (.In_0(n2_1_mux_2_out), .In_1(n2_1_mux_1_out), .Out(Out), .Select(Select_0));
endmodule
