// Logisim project PWM..circ as structural Verilog: 1 circuit, main circuit main
module main (
  input  [1:0] in_1,
  input  [1:0] in_2,
  input  [1:0] in_3,
  input  [1:0] in_4,
  input  [1:0] in_5,
  input  [1:0] in_6,
  input  [1:0] in_7,
  input  [1:0] in_8,
  input  [1:0] in_9,
  input  [1:0] in_10,
  input  [1:0] in_11,
  input  [1:0] in_12
);

  wire clock_1_out, comparator_1_gt, comparator_2_gt, comparator_3_gt, comparator_4_gt, decoder_1_out0,
       decoder_1_out1, decoder_1_out2, decoder_1_out3;
  wire [1:0] counter_1_q, ram_1_data, random_1_out, register_1_q, register_2_q, register_3_q, register_4_q;

  Clock clock_1 (.out(clock_1_out));
  Counter #(.width(2), .max('h3)) counter_1 (.Q(counter_1_q), .clk(clock_1_out));  // open: load, D, count, carry, clr
  Random #(.width(2)) random_1 (.clk(clock_1_out), .out(random_1_out));  // open: next, clr
  RAM #(.addrWidth(2), .dataWidth(2), .bus("separate")) ram_1 (
    .addr(counter_1_q), .din(random_1_out), .data(ram_1_data), .clk(clock_1_out));  // open: str, sel, ld, clr
  Register #(.width(2)) register_1 (.D(ram_1_data), .Q(register_1_q), .clk(decoder_1_out0));  // open: en, clr
  Decoder #(.select(2)) decoder_1 (
    .out0(decoder_1_out0), .out1(decoder_1_out1), .out2(decoder_1_out2), .out3(decoder_1_out3),
    .sel(counter_1_q));  // open: en
  Multiplexer #(.width(2)) multiplexer_1 (.in0(in_1), .in1(in_2), .sel(comparator_1_gt));  // open: out, en
  Comparator #(.width(2)) comparator_1 (.a(register_1_q), .b(in_9), .gt(comparator_1_gt));  // open: eq, lt
  Register #(.width(2)) register_2 (.D(ram_1_data), .Q(register_2_q), .clk(decoder_1_out1));  // open: en, clr
  Multiplexer #(.width(2)) multiplexer_2 (.in0(in_3), .in1(in_5), .sel(comparator_2_gt));  // open: out, en
  Comparator #(.width(2)) comparator_2 (.a(register_2_q), .b(in_10), .gt(comparator_2_gt));  // open: eq, lt
  Register #(.width(2)) register_3 (.D(ram_1_data), .Q(register_3_q), .clk(decoder_1_out2));  // open: en, clr
  Multiplexer #(.width(2)) multiplexer_3 (.in0(in_4), .in1(in_6), .sel(comparator_3_gt));  // open: out, en
  Comparator #(.width(2)) comparator_3 (.a(register_3_q), .b(in_11), .gt(comparator_3_gt));  // open: eq, lt
  Register #(.width(2)) register_4 (.D(ram_1_data), .Q(register_4_q), .clk(decoder_1_out3));  // open: en, clr
  Multiplexer #(.width(2)) multiplexer_4 (.in0(in_7), .in1(in_8), .sel(comparator_4_gt));  // open: out, en
  Comparator #(.width(2)) comparator_4 (.a(register_4_q), .b(in_12), .gt(comparator_4_gt));  // open: eq, lt
endmodule
